// Logisim project ControlUnit.circ as structural Verilog: 1 circuit, main circuit Control Unit
module Control_Unit (
  input  [19:0] I,
  input  C,
  output F
);

  wire n3bitregister_1_p2, n3bitregister_1_p3;
  wire [2:0] n3bitregister_1_p4;

  // _3BitRegister 3bitregister_1: pin names not known; wires that end beside it: C, n3bitregister_1_p2, n3bitregister_1_p3, n3bitregister_1_p4
  Decoder #(.select(3), .disabled(0), .enable("false")) decoder_1 (
    .out0(F), .sel(n3bitregister_1_p4));  // open: out1, out2, out3, out4, out5, out6, out7

  // Notes on the sheet:
  //   F: pull=down
endmodule
